# Fritzing sketch BerryMetre (saved by Fritzing 0.9.9b)
circuit board: 12cm x 8cm
breadboards: 1

parts:
  Q1 = NPN-Transistor [package="TO92 [THT]"]
  R1 = Resistor [tolerance=±5% power=0.25 resistance=0 package=THT]
  R2 = Resistor [tolerance=±5% power=0.25 resistance=330 package=THT]
  Part1 = Arduino Pro Mini v13
  Q2 = NPN-Transistor [package="TO92 [THT]"]
  R3 = Resistor [tolerance=±5% power=0.25 resistance=120 package=THT]
  R4 = Resistor [tolerance=±5% power=0.25 resistance=330 package=THT]
  Q3 = NPN-Transistor [package="TO92 [THT]"]
  R5 = Resistor [tolerance=±5% power=0.25 resistance=380 package=THT]
  R6 = Resistor [tolerance=±5% power=0.25 resistance=330 package=THT]
  Q4 = NPN-Transistor [package="TO92 [THT]"]
  R7 = Resistor [tolerance=±5% power=0.25 resistance=800 package=THT]
  R8 = Resistor [tolerance=±5% power=0.25 resistance=330 package=THT]
  Q5 = NPN-Transistor [package="TO92 [THT]"]
  R9 = Resistor [tolerance=±5% power=0.25 resistance=1k package=THT]
  R10 = Resistor [tolerance=±5% power=0.25 resistance=330 package=THT]
  Q6 = NPN-Transistor [package="TO92 [THT]"]
  R11 = Resistor [tolerance=±5% power=0.25 resistance=1.5k package=THT]
  R12 = Resistor [tolerance=±5% power=0.25 resistance=330 package=THT]
  Q7 = NPN-Transistor [package="TO92 [THT]"]
  R13 = Resistor [tolerance=±5% power=0.25 resistance=2.2k package=THT]
  R14 = Resistor [tolerance=±5% power=0.25 resistance=330 package=THT]
  Q8 = NPN-Transistor [package="TO92 [THT]"]
  R15 = Resistor [tolerance=±5% power=0.25 resistance=3.3k package=THT]
  R16 = Resistor [tolerance=±5% power=0.25 resistance=330 package=THT]
  Q9 = NPN-Transistor [package="TO92 [THT]"]
  R17 = Resistor [tolerance=±5% power=0.25 resistance=4.7k package=THT]
  R18 = Resistor [tolerance=±5% power=0.25 resistance=330 package=THT]
  Q10 = NPN-Transistor [package="TO92 [THT]"]
  R19 = Resistor [tolerance=±5% power=0.25 resistance=5.5k package=THT]
  R20 = Resistor [tolerance=±5% power=0.25 resistance=330 package=THT]
  Q11 = NPN-Transistor [package="TO92 [THT]"]
  R21 = Resistor [tolerance=±5% power=0.25 resistance=27k package=THT]
  R22 = Resistor [tolerance=±5% power=0.25 resistance=330 package=THT]
  Q12 = NPN-Transistor [package="TO92 [THT]"]
  R23 = Resistor [tolerance=±5% power=0.25 resistance=120k package=THT]
  R24 = Resistor [tolerance=±5% power=0.25 resistance=330 package=THT]
  WeMos_D1_Mini1 = WeMos D1 Mini
  VCC2 = Battery
  J1 = female pin header, 2 pins [form="♀ (female)"]
  J2 = female pin header, 2 pins [form="♀ (female)"]
  VCC1 = Battery
  S1 = Toggle Switch [package=THT]
  S2 = Toggle Switch [package=THT]

nets:
  N1: Q1.E, R1.Pin_0
  N2: Q1.B, R2.Pin_0
  N3: Q1.C, Part1.GND, Q2.C, Q3.C, Q4.C, Q5.C, Q6.C, Q7.C, Q8.C, Q9.C, Q10.C, Q11.C, Q12.C, WeMos_D1_Mini1.G, VCC2.-, J1.pin1, J1.pin2, VCC1.-
  N4: R1.Pin_1, Part1.A2, R3.Pin_1, R5.Pin_1, R7.Pin_1, R9.Pin_1, R11.Pin_1, R13.Pin_1, R15.Pin_1, R17.Pin_1, R19.Pin_1, R21.Pin_1, R23.Pin_1, J2.pin1, J2.pin2
  N5: R2.Pin_1, Part1.A0
  N6: Part1.D0/TX, S2.L1
  N7: Part1.D1/RX, S1.L1
  N8: Part1.VCC, VCC1.+
  N9: Part1.D12/MISO, R4.Pin_1
  N10: Part1.D11_PWM/MOSI, R6.Pin_1
  N11: Part1.D10_PWM/SS, R8.Pin_1
  N12: Part1.D9_PWM, R10.Pin_1
  N13: Part1.D8, R12.Pin_1
  N14: Part1.D7, R14.Pin_1
  N15: Part1.D6_PWM, R16.Pin_1
  N16: Part1.D5_PWM, R18.Pin_1
  N17: Part1.D4, R20.Pin_1
  N18: Part1.D3_PWM, R22.Pin_1
  N19: Part1.D2, R24.Pin_1
  N20: Q2.E, R3.Pin_0
  N21: Q2.B, R4.Pin_0
  N22: Q3.E, R5.Pin_0
  N23: Q3.B, R6.Pin_0
  N24: Q4.E, R7.Pin_0
  N25: Q4.B, R8.Pin_0
  N26: Q5.E, R9.Pin_0
  N27: Q5.B, R10.Pin_0
  N28: Q6.E, R11.Pin_0
  N29: Q6.B, R12.Pin_0
  N30: Q7.E, R13.Pin_0
  N31: Q7.B, R14.Pin_0
  N32: Q8.E, R15.Pin_0
  N33: Q8.B, R16.Pin_0
  N34: Q9.E, R17.Pin_0
  N35: Q9.B, R18.Pin_0
  N36: Q10.E, R19.Pin_0
  N37: Q10.B, R20.Pin_0
  N38: Q11.E, R21.Pin_0
  N39: Q11.B, R22.Pin_0
  N40: Q12.E, R23.Pin_0
  N41: Q12.B, R24.Pin_0
  N42: WeMos_D1_Mini1.3V3, VCC2.+
  N43: WeMos_D1_Mini1.RX, S2.COM
  N44: WeMos_D1_Mini1.TX, S1.COM
